# Fritzing sketch CO2_Ampel_Teensy_Neopixel_OLED (saved by Fritzing 0.9.4)

parts:
  Part1 = SCD30
  Teensy_LC1 = Teensy-LC
  Part2 = NeoPixel Stick [part_number=1426]
  R1 = Resistor [tolerance=±5% resistance=330 package=THT]
  OLED1 = 128x32 I2C Monochrome OLED Display
  RE1 = Hexadecimal Rotary Encoder [part_number=APEM-PT65-303 package=THT]

nets:
  VDD: Part1.VDD, Teensy_LC1.3V3, OLED1.3.3V
  GND: Part1.GND, Teensy_LC1.AGND, OLED1.GND
  N1: Part1.TX/SCL, Teensy_LC1.A8/D22
  N2: Part1.RX/SDA, Teensy_LC1.A9/D23
  GND_2: Teensy_LC1.GND, Part2.GND, RE1.InputCommon
  N3: Teensy_LC1.D0, RE1.Output1Pin
  N4: Teensy_LC1.D1, RE1.Output2Pin
  N5: Teensy_LC1.D2, RE1.Output4Pin
  N6: Teensy_LC1.D3, RE1.Output8pin
  N7: Teensy_LC1.5Vout, R1.Pin_0
  N8: Teensy_LC1.A4/D18, OLED1.SDA
  N9: Teensy_LC1.A5/D19, OLED1.SCL
  N10: Teensy_LC1.A6/D20, OLED1.RST
  VIN: Teensy_LC1.Vin, Part2.+5V
  N11: Part2.DATAIN, R1.Pin_1

custom parts:
  SCD30: CO2 , humidity, and temperature sensor * Current consumption: 19 mA @ 1 meas. per 2 s. * Digital interface UART or I2C * Company: Sensirion - The Sensor Company Electrical specifications * average current: 19 mA * max. current: 75 mA * DC supply: 3.3 V - 5.5 V Operation conditions * temperature: 0 – 50°C * humidity: 0 – 95 %RH * sensor lifetime: 15 years CO2-sensor: * NDIR CO 2 sensor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
  Teensy-LC: Teensy-LC (Low Cost) is a powerful 32 bit microcontroller board, with a rich set of hardware peripherals, at a very affordable price! Teensy-LC delivers an impressive collection of capabilities to make modern electronic projects simpler. It features an ARM Cortex-M0+ processor at 48 MHz, 62K Flash, 8K RAM, 12 bit analog input & output, hardware Serial, SPI & I2C, USB, and a total of 27 I/O pins.
  NeoPixel Stick: Make your own little LED strip arrangement with this stick of NeoPixel LEDs. We crammed 8 of the tiny 5050 (5mm x 5mm) smart RGB LEDs onto a PCB with mounting holes and a chainable design. Use only one microcontroller pin to control as many as you can chain together! Each LED is addressable as the driver chip is inside the LED. Each one has ~18mA constant current drive so the color will be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
